// Logisim project 4bit_ALU-complete.circ as structural Verilog: 7 circuits, main circuit main
module main (
  input  A0,
  input  A1,
  input  A2,
  input  A3,
  input  B0,
  input  B1,
  input  B2,
  input  B3,
  input  S0,
  input  S1,
  output OUT_0,
  output OUT_1,
  output OUT_2,
  output OUT_3
);

  wire [3:0] ADD, AND, OR, XOR;

  _4bit_bitwise_XOR u_4bit_bitwise_xor_1 (
    .A0(A0), .A1(A1), .A2(A2), .A3(A3), .B0(B0), .B1(B1), .B2(B2), .B3(B3), .F0(XOR[0]), .out_10(XOR[1]),
    .F2(XOR[2]), .F3(XOR[3]));
  _4bit_bitwise_AND u_4bit_bitwise_and_1 (
    .A0(A0), .A1(A1), .A2(A2), .A3(A3), .B0(B0), .B1(B1), .B2(B2), .B3(B3), .F0(AND[0]), .out_10(AND[1]),
    .F2(AND[2]), .F3(AND[3]));
  _4bit_bitwise_OR u_4bit_bitwise_or_1 (
    .A0(A0), .A1(A1), .A2(A2), .A3(A3), .B0(B0), .B1(B1), .B2(B2), .B3(B3), .F0(OR[0]), .out_10(OR[1]),
    .F2(OR[2]), .F3(OR[3]));
  _4bit_bitwise_ADD u_4bit_bitwise_add_1 (
    .A0(A0), .B0(B0), .A1(A1), .B1(B1), .A2(A2), .B2(B2), .A3(A3), .B3(B3), .S0(ADD[0]), .S1(ADD[1]),
    .S2(ADD[2]), .S3(ADD[3]));
  _4Bit_4_1_MUX u_4bit_4_1_mux_1 (
    .AND0(AND[0]), .AND1(AND[1]), .AND2(AND[2]), .AND3(AND[3]), .OR0(OR[0]), .OR1(OR[1]), .OR2(OR[2]),
    .OR3(OR[3]), .XOR0(XOR[0]), .XOR1(XOR[1]), .XOR2(XOR[2]), .XOR3(XOR[3]), .ADD0(ADD[0]), .ADD1(ADD[1]),
    .ADD2(ADD[2]), .ADD3(ADD[3]), .OUT_0(OUT_0), .OUT_1(OUT_1), .OUT_2(OUT_2), .OUT_3(OUT_3), .S0(S0), .S1(S1));
endmodule

module _4bit_bitwise_AND (
  input  A0,
  input  A1,
  input  A2,
  input  A3,
  input  B0,
  input  B1,
  input  B2,
  input  B3,
  output F0,
  output out_10,
  output F2,
  output F3
);

  and and_1 (F0, A0, B0);
  and and_2 (out_10, A1, B1);
  and and_3 (F2, A2, B2);
  and and_4 (F3, A3, B3);

  // Notes on the sheet:
  //   F1
endmodule

module _4bit_bitwise_OR (
  input  A0,
  input  A1,
  input  A2,
  input  A3,
  input  B0,
  input  B1,
  input  B2,
  input  B3,
  output F0,
  output out_10,
  output F2,
  output F3
);

  or or_1 (F0, A0, B0);
  or or_2 (out_10, A1, B1);
  or or_3 (F2, A2, B2);
  or or_4 (F3, A3, B3);

  // Notes on the sheet:
  //   F1
endmodule

module _4bit_bitwise_XOR (
  input  A0,
  input  A1,
  input  A2,
  input  A3,
  input  B0,
  input  B1,
  input  B2,
  input  B3,
  output F0,
  output out_10,
  output F2,
  output F3
);

  xor xor_1 (F0, A0, B0);
  xor xor_2 (out_10, A1, B1);
  xor xor_3 (F2, A2, B2);
  xor xor_4 (F3, A3, B3);

  // Notes on the sheet:
  //   F1
endmodule

module _4bit_bitwise_ADD (
  input  A0,
  input  A1,
  input  A2,
  input  A3,
  input  B0,
  input  B1,
  input  B2,
  input  B3,
  output S0,
  output S1,
  output S2,
  output S3
);

  wire Cin1, Cin2, Cin3, Cin4;

  _2bit_ripple_carry_adder u_2bit_ripple_carry_adder_1 (.A(A0), .B(B0), .Cin(1'b0), .S(S0), .Cout(Cin1));
  _2bit_ripple_carry_adder u_2bit_ripple_carry_adder_2 (.A(A1), .B(B1), .Cin(Cin1), .S(S1), .Cout(Cin2));
  _2bit_ripple_carry_adder u_2bit_ripple_carry_adder_3 (.A(A2), .B(B2), .Cin(Cin2), .S(S2), .Cout(Cin3));
  _2bit_ripple_carry_adder u_2bit_ripple_carry_adder_4 (.A(A3), .B(B3), .Cin(Cin3), .S(S3), .Cout(Cin4));
endmodule

module _2bit_ripple_carry_adder (
  input  A,
  input  B,
  input  Cin,
  output S,
  output Cout
);

  wire and_1_out, and_2_out, and_3_out;

  xor xor_1 (S, A, B, Cin);
  and and_1 (and_1_out, A, B);
  and and_2 (and_2_out, A, Cin);
  and and_3 (and_3_out, B, Cin);
  xor xor_2 (Cout, and_1_out, and_2_out, and_3_out);
endmodule

module _4Bit_4_1_MUX (
  input  XOR0,
  input  XOR1,
  input  XOR2,
  input  XOR3,
  input  AND0,
  input  AND1,
  input  AND2,
  input  AND3,
  input  OR0,
  input  OR1,
  input  OR2,
  input  OR3,
  input  ADD0,
  input  ADD1,
  input  ADD2,
  input  S0,
  input  S1,
  input  ADD3,
  output OUT_0,
  output OUT_1,
  output OUT_2,
  output OUT_3
);

  Multiplexer #(.select(2), .enable("false")) multiplexer_1 (
    .in0(XOR0), .in1(AND0), .in2(OR0), .in3(ADD0), .out(OUT_0), .sel({S1, S0}));
  Multiplexer #(.select(2), .enable("false")) multiplexer_2 (
    .in0(XOR1), .in1(AND1), .in2(OR1), .in3(ADD1), .out(OUT_1), .sel({S1, S0}));
  Multiplexer #(.select(2), .enable("false")) multiplexer_3 (
    .in0(XOR2), .in1(AND2), .in2(OR2), .in3(ADD2), .out(OUT_2), .sel({S1, S0}));
  Multiplexer #(.select(2), .enable("false")) multiplexer_4 (
    .in0(XOR3), .in1(AND3), .in2(OR3), .in3(ADD3), .out(OUT_3), .sel({S1, S0}));

  // Other names for the same wires on the sheet: OUT0 = OUT_0; OUT1 = OUT_1; OUT2 = OUT_2; OUT3 = OUT_3
endmodule
